// Logisim project pg58.circ as structural Verilog: 1 circuit, main circuit main
module main (
  input  x
);

  wire A_q, and_1_out, and_2_out, B_q, Clock_out, not_1_out, xnor_1_out;

  not not_1 (not_1_out, x);
  and and_1 (and_1_out, B_q, not_1_out);
  and and_2 (and_2_out, B_q, x);
  xnor xnor_1 (xnor_1_out, A_q, x);
  Clock Clock (.out(Clock_out));
  J_K_Flip_Flop A (.J(and_1_out), .clk(Clock_out), .K(and_2_out), .Q(A_q));  // open: Qn, preset, en, reset
  J_K_Flip_Flop B (.J(x), .clk(Clock_out), .K(xnor_1_out), .Q(B_q));  // open: Qn, preset, en, reset
endmodule
