// Logisim project pg60.circ as structural Verilog: 1 circuit, main circuit main
module main (
  input  X,
  output Y
);

  wire A_q, A_qn, and_2_out, and_3_out, and_4_out, and_5_out, and_6_out, B_q, B_qn, Clock_out, not_1_out,
       or_1_out, or_2_out;

  not not_1 (not_1_out, X);
  and and_1 (Y, B_qn, X);
  and and_2 (and_2_out, A_q, B_qn);
  or or_1 (or_1_out, and_2_out, and_3_out);
  and and_3 (and_3_out, B_q, not_1_out);
  and and_4 (and_4_out, A_qn, X);
  or or_2 (or_2_out, and_4_out, and_5_out, and_6_out);
  and and_5 (and_5_out, B_qn, X);
  and and_6 (and_6_out, A_q, B_q, not_1_out);
  Clock Clock (.out(Clock_out));
  D_Flip_Flop A (.clk(Clock_out), .D(or_1_out), .Q(A_q), .Qn(A_qn));  // open: preset, en, reset
  D_Flip_Flop B (.clk(Clock_out), .D(or_2_out), .Q(B_q), .Qn(B_qn));  // open: preset, en, reset
endmodule
